// Logisim project alu.circ as structural Verilog: 1 circuit, main circuit main
module main (
  input  [15:0] a_in,
  input  [15:0] b_in,
  input  [3:0] opcode,
  output [15:0] final_output,
  output error
);

  wire adder_1_cout, clk_out, nor_1_out, not_1_out, or_1_out, reset_out, subtractor_1_bout;
  wire [3:0] b_reg_q, selector_q;
  wire [11:0] b_reg_q_2;
  wire [15:0] a_reg_q, adder_1_out, and_test_out, bit_extender_1_out, bit_extender_2_out, divider_1_rem,
       divider_2_out, multiplexer_1_out, multiplier_1_cout, multiplier_1_out, nand_test_out, nor_test_out,
       not_test_out, or_test_out, shifter_1_out, shifter_2_out, subtractor_1_out, xnor_test_out, xor_test_out;

  nor nor_1 (nor_1_out, b_reg_q_2[3], b_reg_q[0], b_reg_q[1], b_reg_q[2], b_reg_q[3], b_reg_q_2[0], b_reg_q_2[1], b_reg_q_2[2], b_reg_q_2[4], b_reg_q_2[5], b_reg_q_2[6], b_reg_q_2[7], b_reg_q_2[8], b_reg_q_2[9], b_reg_q_2[10], b_reg_q_2[11]);
  Clock clk (.out(clk_out));
  and reset (reset_out, selector_q[0], selector_q[1], selector_q[3], selector_q[2]);
  assign bit_extender_1_out = {{15{1'b0}}, 1'b0};  // Bit_Extender bit_extender_1
  Register #(.width(16)) a_reg (.D(a_in), .Q(a_reg_q), .clk(clk_out), .clr(reset_out));  // open: en
  Register #(.width(16)) b_reg (.D(b_in), .Q({b_reg_q_2, b_reg_q}), .clk(clk_out), .clr(reset_out));  // open: en
  Register #(.width(4)) selector (.D(opcode), .Q(selector_q), .clk(clk_out), .clr(1'b0));  // open: en
  assign and_test_out = a_reg_q & {b_reg_q_2, b_reg_q};  // AND_Gate and_test, 16 bits wide
  assign or_test_out = a_reg_q | {b_reg_q_2, b_reg_q};  // OR_Gate or_test, 16 bits wide
  assign xor_test_out = a_reg_q ^ {b_reg_q_2, b_reg_q};  // XOR_Gate xor_test, 16 bits wide
  Adder #(.width(16)) adder_1 (
    .a(a_reg_q), .b({b_reg_q_2, b_reg_q}), .out(adder_1_out), .cin(1'b0), .cout(adder_1_cout));
  Multiplier #(.width(16)) multiplier_1 (
    .a(a_reg_q), .b({b_reg_q_2, b_reg_q}), .out(multiplier_1_out), .cin(bit_extender_1_out),
    .cout(multiplier_1_cout));
  Shifter #(.width(16), .shift("lr")) shifter_1 (.in(a_reg_q), .\dist (b_reg_q), .out(shifter_1_out));
  assign not_test_out = ~a_reg_q;  // NOT_Gate not_test, 16 bits wide
  Divider #(.width(16)) divider_1 (.a(a_reg_q), .b({b_reg_q_2, b_reg_q}), .rem(divider_1_rem));  // open: out, upper
  assign nand_test_out = ~(a_reg_q & {b_reg_q_2, b_reg_q});  // NAND_Gate nand_test, 16 bits wide
  assign nor_test_out = ~(a_reg_q | {b_reg_q_2, b_reg_q});  // NOR_Gate nor_test, 16 bits wide
  not not_1 (not_1_out, reset_out);
  assign xnor_test_out = ~(a_reg_q ^ {b_reg_q_2, b_reg_q});  // XNOR_Gate xnor_test, 16 bits wide
  assign bit_extender_2_out = {{15{1'b0}}, not_1_out};  // Bit_Extender bit_extender_2
  Multiplexer #(.select(4), .width(16), .disabled(0), .enable("false")) multiplexer_1 (
    .in0(final_output), .in1(and_test_out), .in2(or_test_out), .in3(xor_test_out), .in4(adder_1_out),
    .in5(multiplier_1_out), .in6(shifter_1_out), .in7(not_test_out), .in8(divider_1_rem),
    .in9(nand_test_out), .in10(nor_test_out), .in11(xnor_test_out), .in12(subtractor_1_out),
    .in13(divider_2_out), .in14(shifter_2_out), .in15(bit_extender_2_out), .out(multiplexer_1_out),
    .sel(selector_q));
  Subtractor #(.width(16)) subtractor_1 (
    .a(a_reg_q), .b({b_reg_q_2, b_reg_q}), .out(subtractor_1_out), .bin(1'b0), .bout(subtractor_1_bout));
  Register #(.width(16)) pers_op (.D(multiplexer_1_out), .Q(final_output), .clk(clk_out), .clr(reset_out));  // open: en
  or or_1 (or_1_out, multiplier_1_cout[0], multiplier_1_cout[1], multiplier_1_cout[2], multiplier_1_cout[3], multiplier_1_cout[4], multiplier_1_cout[5], multiplier_1_cout[6], multiplier_1_cout[7], multiplier_1_cout[8], multiplier_1_cout[9], multiplier_1_cout[10], multiplier_1_cout[11], multiplier_1_cout[12], multiplier_1_cout[13], multiplier_1_cout[14], multiplier_1_cout[15]);
  Divider #(.width(16)) divider_2 (.a(a_reg_q), .b({b_reg_q_2, b_reg_q}), .out(divider_2_out));  // open: upper, rem
  Shifter #(.width(16)) shifter_2 (.in(a_reg_q), .\dist (b_reg_q), .out(shifter_2_out));
  Multiplexer #(.select(4), .disabled(0), .enable("false")) multiplexer_2 (
    .in0(1'b0), .in1(1'b0), .in2(1'b0), .in3(1'b0), .in4(adder_1_cout), .in5(or_1_out), .in6(1'b0),
    .in7(1'b0), .in8(nor_1_out), .in9(1'b0), .in10(1'b0), .in11(1'b0), .in12(subtractor_1_bout),
    .in13(nor_1_out), .in14(1'b0), .in15(1'b0), .out(error), .sel(selector_q));

  // Notes on the sheet:
  //   Test for divide by 0
  //   a
  //   b
  //   SRL
  //   Modulus
  //   out[0] through out[15]
  //   Addition overflow check
  //   Multiplication overflow check
  //   Divide
  //   SLL
endmodule
